// Logisim project 8bitCalc.circ as structural Verilog
module FA (
  input  in_1,
  input  in_2,
  input  in_3,
  output out_4,
  output out_5
);

  wire and_1_out, and_2_out, xor_1_out;

  xor xor_1 (xor_1_out, in_1, in_2);
  and and_1 (and_1_out, in_1, in_2);
  xor xor_2 (out_4, xor_1_out, in_3);
  and and_2 (and_2_out, xor_1_out, in_3);
  or or_1 (out_5, and_2_out, and_1_out);
endmodule

module PU (
  input  in_1,
  input  in_2,
  input  in_3,
  input  in_4,
  output out_5,
  output out_6
);

  wire fa_1_out_4, not_1_out;

  not not_1 (not_1_out, in_2);
  Multiplexer multiplexer_1 (.in0(in_1), .in1(fa_1_out_4), .out(out_6), .sel(in_4));  // open: en
  FA fa_1 (.in_1(in_1), .in_2(not_1_out), .in_3(in_3), .out_4(fa_1_out_4), .out_5(out_5));
endmodule

module _8_bit_div (
  input  in_1,
  input  in_2,
  input  in_3,
  input  in_4,
  input  in_5,
  input  in_6,
  input  in_7,
  input  in_8,
  input  in_9,
  input  in_10,
  input  in_11,
  input  in_12,
  input  in_13,
  input  in_14,
  input  in_15,
  input  in_16,
  input  in_17,
  input  in_18,
  input  in_19,
  input  in_20,
  input  in_21,
  input  in_22,
  input  in_23,
  input  in_24,
  input  in_25,
  output out_26,
  output out_27,
  output out_28,
  output out_29,
  output out_30,
  output out_31,
  output out_32,
  output out_33,
  output out_34,
  output out_35,
  output out_36,
  output out_37,
  output out_38,
  output out_39,
  output out_40,
  output out_41
);

  wire pu_2_out_5, pu_2_out_6, pu_3_out_5, pu_3_out_6, pu_4_out_5, pu_4_out_6, pu_7_out_5, pu_7_out_6,
       pu_8_out_5, pu_8_out_6, pu_9_out_5, pu_9_out_6, pu_11_out_5, pu_11_out_6, pu_12_out_5, pu_12_out_6,
       pu_13_out_5, pu_13_out_6, pu_14_out_5, pu_14_out_6, pu_16_out_5, pu_16_out_6, pu_17_out_5,
       pu_17_out_6, pu_18_out_5, pu_18_out_6, pu_19_out_5, pu_19_out_6, pu_20_out_5, pu_20_out_6,
       pu_22_out_5, pu_22_out_6, pu_23_out_5, pu_23_out_6, pu_24_out_5, pu_24_out_6, pu_25_out_5,
       pu_25_out_6, pu_26_out_5, pu_26_out_6, pu_27_out_5, pu_27_out_6, pu_29_out_5, pu_29_out_6,
       pu_30_out_5, pu_30_out_6, pu_31_out_5, pu_31_out_6, pu_32_out_5, pu_32_out_6, pu_33_out_5,
       pu_33_out_6, pu_34_out_5, pu_34_out_6, pu_35_out_5, pu_35_out_6, pu_36_out_5, pu_36_out_6,
       pu_37_out_5, pu_37_out_6, pu_38_out_5, pu_38_out_6, pu_39_out_5, pu_39_out_6, pu_40_out_5,
       pu_40_out_6, pu_42_out_5, pu_42_out_6, pu_43_out_5, pu_43_out_6, pu_44_out_5, pu_44_out_6,
       pu_45_out_5, pu_45_out_6, pu_46_out_5, pu_46_out_6, pu_47_out_5, pu_47_out_6, pu_48_out_5,
       pu_49_out_5, pu_50_out_5, pu_50_out_6, pu_51_out_5, pu_51_out_6, pu_52_out_5, pu_52_out_6,
       pu_53_out_5, pu_53_out_6, pu_54_out_5, pu_55_out_5, pu_55_out_6, pu_56_out_5, pu_56_out_6,
       pu_57_out_5, pu_57_out_6, pu_58_out_5, pu_59_out_5, pu_59_out_6, pu_60_out_5, pu_60_out_6,
       pu_61_out_5, pu_62_out_5, pu_62_out_6, pu_63_out_5, pu_64_out_5;

  PU pu_1 (.in_1(in_17), .in_2(in_1), .in_3(pu_2_out_5), .out_5(out_26), .in_4(out_26));  // open: out_6
  PU pu_2 (.in_1(in_17), .in_2(in_2), .in_3(pu_3_out_5), .out_6(pu_2_out_6), .out_5(pu_2_out_5), .in_4(out_26));
  PU pu_3 (.in_1(in_17), .in_2(in_3), .in_3(pu_7_out_5), .out_6(pu_3_out_6), .out_5(pu_3_out_5), .in_4(out_26));
  PU pu_4 (.in_1(pu_3_out_6), .in_2(in_2), .in_3(pu_8_out_5), .out_6(pu_4_out_6), .out_5(pu_4_out_5), .in_4(out_27));
  PU pu_5 (.in_1(pu_2_out_6), .in_2(in_1), .in_3(pu_4_out_5), .out_5(out_27), .in_4(out_27));  // open: out_6
  PU pu_6 (.in_1(pu_4_out_6), .in_2(in_1), .in_3(pu_9_out_5), .out_5(out_28), .in_4(out_28));  // open: out_6
  PU pu_7 (.in_1(in_17), .in_2(in_4), .in_3(pu_11_out_5), .out_6(pu_7_out_6), .out_5(pu_7_out_5), .in_4(out_26));
  PU pu_8 (.in_1(pu_7_out_6), .in_2(in_3), .in_3(pu_12_out_5), .out_6(pu_8_out_6), .out_5(pu_8_out_5), .in_4(out_27));
  PU pu_9 (.in_1(pu_8_out_6), .in_2(in_2), .in_3(pu_13_out_5), .out_6(pu_9_out_6), .out_5(pu_9_out_5), .in_4(out_28));
  PU pu_10 (.in_1(pu_9_out_6), .in_2(in_1), .in_3(pu_14_out_5), .out_5(out_29), .in_4(out_29));  // open: out_6
  PU pu_11 (.in_1(in_17), .in_2(in_5), .in_3(pu_16_out_5), .out_6(pu_11_out_6), .out_5(pu_11_out_5), .in_4(out_26));
  PU pu_12 (
    .in_1(pu_11_out_6), .in_2(in_4), .in_3(pu_17_out_5), .out_6(pu_12_out_6), .out_5(pu_12_out_5),
    .in_4(out_27));
  PU pu_13 (
    .in_1(pu_12_out_6), .in_2(in_3), .in_3(pu_18_out_5), .out_6(pu_13_out_6), .out_5(pu_13_out_5),
    .in_4(out_28));
  PU pu_14 (
    .in_1(pu_13_out_6), .in_2(in_2), .in_3(pu_19_out_5), .out_6(pu_14_out_6), .out_5(pu_14_out_5),
    .in_4(out_29));
  PU pu_15 (.in_1(pu_14_out_6), .in_2(in_1), .in_3(pu_20_out_5), .out_5(out_30), .in_4(out_30));  // open: out_6
  PU pu_16 (.in_1(in_17), .in_2(in_6), .in_3(pu_22_out_5), .out_6(pu_16_out_6), .out_5(pu_16_out_5), .in_4(out_26));
  PU pu_17 (
    .in_1(pu_16_out_6), .in_2(in_5), .in_3(pu_23_out_5), .out_6(pu_17_out_6), .out_5(pu_17_out_5),
    .in_4(out_27));
  PU pu_18 (
    .in_1(pu_17_out_6), .in_2(in_4), .in_3(pu_24_out_5), .out_6(pu_18_out_6), .out_5(pu_18_out_5),
    .in_4(out_28));
  PU pu_19 (
    .in_1(pu_18_out_6), .in_2(in_3), .in_3(pu_25_out_5), .out_6(pu_19_out_6), .out_5(pu_19_out_5),
    .in_4(out_29));
  PU pu_20 (
    .in_1(pu_19_out_6), .in_2(in_2), .in_3(pu_26_out_5), .out_6(pu_20_out_6), .out_5(pu_20_out_5),
    .in_4(out_30));
  PU pu_21 (.in_1(pu_20_out_6), .in_2(in_1), .in_3(pu_27_out_5), .out_5(out_31), .in_4(out_31));  // open: out_6
  PU pu_22 (.in_1(in_17), .in_2(in_7), .in_3(pu_29_out_5), .out_6(pu_22_out_6), .out_5(pu_22_out_5), .in_4(out_26));
  PU pu_23 (
    .in_1(pu_22_out_6), .in_2(in_6), .in_3(pu_30_out_5), .out_6(pu_23_out_6), .out_5(pu_23_out_5),
    .in_4(out_27));
  PU pu_24 (
    .in_1(pu_23_out_6), .in_2(in_5), .in_3(pu_33_out_5), .out_6(pu_24_out_6), .out_5(pu_24_out_5),
    .in_4(out_28));
  PU pu_25 (
    .in_1(pu_24_out_6), .in_2(in_4), .in_3(pu_35_out_5), .out_6(pu_25_out_6), .out_5(pu_25_out_5),
    .in_4(out_29));
  PU pu_26 (
    .in_1(pu_25_out_6), .in_2(in_3), .in_3(pu_37_out_5), .out_6(pu_26_out_6), .out_5(pu_26_out_5),
    .in_4(out_30));
  PU pu_27 (
    .in_1(pu_26_out_6), .in_2(in_2), .in_3(pu_39_out_5), .out_6(pu_27_out_6), .out_5(pu_27_out_5),
    .in_4(out_31));
  PU pu_28 (.in_1(pu_27_out_6), .in_2(in_1), .in_3(pu_40_out_5), .out_5(out_32), .in_4(out_32));  // open: out_6
  PU pu_29 (.in_1(in_9), .in_2(in_8), .in_3(in_18), .out_6(pu_29_out_6), .out_5(pu_29_out_5), .in_4(out_26));
  PU pu_30 (
    .in_1(pu_29_out_6), .in_2(in_7), .in_3(pu_31_out_5), .out_6(pu_30_out_6), .out_5(pu_30_out_5),
    .in_4(out_27));
  PU pu_31 (.in_1(in_10), .in_2(in_8), .in_3(in_19), .out_6(pu_31_out_6), .out_5(pu_31_out_5), .in_4(out_27));
  PU pu_32 (
    .in_1(pu_31_out_6), .in_2(in_7), .in_3(pu_42_out_5), .out_6(pu_32_out_6), .out_5(pu_32_out_5),
    .in_4(out_28));
  PU pu_33 (
    .in_1(pu_30_out_6), .in_2(in_6), .in_3(pu_32_out_5), .out_6(pu_33_out_6), .out_5(pu_33_out_5),
    .in_4(out_28));
  PU pu_34 (
    .in_1(pu_32_out_6), .in_2(in_6), .in_3(pu_43_out_5), .out_6(pu_34_out_6), .out_5(pu_34_out_5),
    .in_4(out_29));
  PU pu_35 (
    .in_1(pu_33_out_6), .in_2(in_5), .in_3(pu_34_out_5), .out_6(pu_35_out_6), .out_5(pu_35_out_5),
    .in_4(out_29));
  PU pu_36 (
    .in_1(pu_34_out_6), .in_2(in_5), .in_3(pu_44_out_5), .out_6(pu_36_out_6), .out_5(pu_36_out_5),
    .in_4(out_30));
  PU pu_37 (
    .in_1(pu_35_out_6), .in_2(in_4), .in_3(pu_36_out_5), .out_6(pu_37_out_6), .out_5(pu_37_out_5),
    .in_4(out_30));
  PU pu_38 (
    .in_1(pu_36_out_6), .in_2(in_4), .in_3(pu_45_out_5), .out_6(pu_38_out_6), .out_5(pu_38_out_5),
    .in_4(out_31));
  PU pu_39 (
    .in_1(pu_37_out_6), .in_2(in_3), .in_3(pu_38_out_5), .out_6(pu_39_out_6), .out_5(pu_39_out_5),
    .in_4(out_31));
  PU pu_40 (
    .in_1(pu_39_out_6), .in_2(in_2), .in_3(pu_47_out_5), .out_6(pu_40_out_6), .out_5(pu_40_out_5),
    .in_4(out_32));
  PU pu_41 (.in_1(pu_40_out_6), .in_2(in_1), .in_3(pu_49_out_5), .out_6(out_34), .out_5(out_33), .in_4(out_33));
  PU pu_42 (.in_1(in_11), .in_2(in_8), .in_3(in_20), .out_6(pu_42_out_6), .out_5(pu_42_out_5), .in_4(out_28));
  PU pu_43 (
    .in_1(pu_42_out_6), .in_2(in_7), .in_3(pu_50_out_5), .out_6(pu_43_out_6), .out_5(pu_43_out_5),
    .in_4(out_29));
  PU pu_44 (
    .in_1(pu_43_out_6), .in_2(in_6), .in_3(pu_51_out_5), .out_6(pu_44_out_6), .out_5(pu_44_out_5),
    .in_4(out_30));
  PU pu_45 (
    .in_1(pu_44_out_6), .in_2(in_5), .in_3(pu_52_out_5), .out_6(pu_45_out_6), .out_5(pu_45_out_5),
    .in_4(out_31));
  PU pu_46 (
    .in_1(pu_45_out_6), .in_2(in_4), .in_3(pu_53_out_5), .out_6(pu_46_out_6), .out_5(pu_46_out_5),
    .in_4(out_32));
  PU pu_47 (
    .in_1(pu_38_out_6), .in_2(in_3), .in_3(pu_46_out_5), .out_6(pu_47_out_6), .out_5(pu_47_out_5),
    .in_4(out_32));
  PU pu_48 (.in_1(pu_46_out_6), .in_2(in_3), .in_3(pu_54_out_5), .out_6(out_36), .out_5(pu_48_out_5), .in_4(out_33));
  PU pu_49 (.in_1(pu_47_out_6), .in_2(in_2), .in_3(pu_48_out_5), .out_6(out_35), .out_5(pu_49_out_5), .in_4(out_33));
  PU pu_50 (.in_1(in_12), .in_2(in_8), .in_3(in_21), .out_6(pu_50_out_6), .out_5(pu_50_out_5), .in_4(out_29));
  PU pu_51 (
    .in_1(pu_50_out_6), .in_2(in_7), .in_3(pu_55_out_5), .out_6(pu_51_out_6), .out_5(pu_51_out_5),
    .in_4(out_30));
  PU pu_52 (
    .in_1(pu_51_out_6), .in_2(in_6), .in_3(pu_56_out_5), .out_6(pu_52_out_6), .out_5(pu_52_out_5),
    .in_4(out_31));
  PU pu_53 (
    .in_1(pu_52_out_6), .in_2(in_5), .in_3(pu_57_out_5), .out_6(pu_53_out_6), .out_5(pu_53_out_5),
    .in_4(out_32));
  PU pu_54 (.in_1(pu_53_out_6), .in_2(in_4), .in_3(pu_58_out_5), .out_6(out_37), .out_5(pu_54_out_5), .in_4(out_33));
  PU pu_55 (.in_1(in_13), .in_2(in_8), .in_3(in_22), .out_6(pu_55_out_6), .out_5(pu_55_out_5), .in_4(out_30));
  PU pu_56 (
    .in_1(pu_55_out_6), .in_2(in_7), .in_3(pu_59_out_5), .out_6(pu_56_out_6), .out_5(pu_56_out_5),
    .in_4(out_31));
  PU pu_57 (
    .in_1(pu_56_out_6), .in_2(in_6), .in_3(pu_60_out_5), .out_6(pu_57_out_6), .out_5(pu_57_out_5),
    .in_4(out_32));
  PU pu_58 (.in_1(pu_57_out_6), .in_2(in_5), .in_3(pu_61_out_5), .out_6(out_38), .out_5(pu_58_out_5), .in_4(out_33));
  PU pu_59 (.in_1(in_14), .in_2(in_8), .in_3(in_23), .out_6(pu_59_out_6), .out_5(pu_59_out_5), .in_4(out_31));
  PU pu_60 (
    .in_1(pu_59_out_6), .in_2(in_7), .in_3(pu_62_out_5), .out_6(pu_60_out_6), .out_5(pu_60_out_5),
    .in_4(out_32));
  PU pu_61 (.in_1(pu_60_out_6), .in_2(in_6), .in_3(pu_63_out_5), .out_6(out_39), .out_5(pu_61_out_5), .in_4(out_33));
  PU pu_62 (.in_1(in_15), .in_2(in_8), .in_3(in_24), .out_6(pu_62_out_6), .out_5(pu_62_out_5), .in_4(out_32));
  PU pu_63 (.in_1(pu_62_out_6), .in_2(in_7), .in_3(pu_64_out_5), .out_6(out_40), .out_5(pu_63_out_5), .in_4(out_33));
  PU pu_64 (.in_1(in_16), .in_2(in_8), .in_3(in_25), .out_6(out_41), .out_5(pu_64_out_5), .in_4(out_33));

  // Other names for the same wires on the sheet: _1 = in_16; _2 = in_15; _3 = in_14; _4 = in_13; _5 = in_12;
  //   _6 = in_11; _7 = in_10; _8 = in_9; D1 = in_8; D2 = in_7; D3 = in_6; D4 = in_5; D5 = in_4; D6 = in_3; D7 = in_2;
  //   D8 = in_1
endmodule

module _16bitadder (
  input  [15:0] in_1,
  input  in_2,
  input  in_3,
  input  [15:0] in_4,
  input  in_5,
  output out_6,
  output [15:0] out_7,
  output out_8
);

  wire and_1_out, and_2_out, and_3_out, and_4_out, and_5_out, and_6_out, and_7_out, and_8_out, and_9_out,
       and_10_out, and_11_out, and_12_out, and_13_out, and_14_out, and_15_out, and_16_out, and_17_out,
       and_18_out, and_19_out, and_20_out, and_21_out, and_22_out, and_23_out, and_24_out, and_25_out,
       and_26_out, and_27_out, and_28_out, and_29_out, and_30_out, and_31_out, and_32_out, and_33_out,
       and_34_out, and_35_out, and_36_out, and_37_out, and_38_out, and_39_out, and_40_out, and_41_out,
       and_42_out, and_43_out, and_44_out, and_45_out, and_46_out, and_47_out, and_48_out, and_49_out,
       and_50_out, and_51_out, and_52_out, and_53_out, and_54_out, and_55_out, and_56_out, fa_1_out_5,
       fa_2_out_5, fa_3_out_5, fa_4_out_5, fa_5_out_5, fa_6_out_5, fa_7_out_5, not_1_out, not_2_out,
       not_3_out, not_4_out, not_5_out, not_6_out, not_7_out, not_8_out, not_9_out, not_10_out, or_1_out,
       or_2_out, or_3_out, or_4_out, or_5_out, or_6_out, or_7_out, or_8_out, or_9_out, or_10_out, or_11_out,
       or_12_out, or_13_out, or_14_out, or_15_out, xor_2_out, xor_3_out, xor_4_out, xor_5_out, xor_6_out,
       xor_7_out, xor_8_out, xor_9_out, xor_10_out, xor_11_out, xor_12_out, xor_13_out, xor_14_out,
       xor_15_out, xor_16_out, xor_17_out;
  wire [7:0] fa_1_out_4;
  wire [15:0] xor_1_out, xor_18_out;

  assign xor_1_out = in_4 ^ {{8{in_5}}, {8{in_2}}};  // XOR_Gate xor_1, 16 bits wide
  xor xor_2 (xor_2_out, in_1[0], xor_1_out[0]);
  and and_1 (and_1_out, in_1[0], xor_1_out[0]);
  xor xor_3 (xor_3_out, in_1[1], xor_1_out[1]);
  and and_2 (and_2_out, in_1[1], xor_1_out[1]);
  xor xor_4 (xor_4_out, in_1[2], xor_1_out[2]);
  and and_3 (and_3_out, in_1[2], xor_1_out[2]);
  xor xor_5 (xor_5_out, in_1[3], xor_1_out[3]);
  and and_4 (and_4_out, in_1[3], xor_1_out[3]);
  and and_5 (and_5_out, in_1[4], xor_1_out[4]);
  xor xor_6 (xor_6_out, in_1[5], xor_1_out[5]);
  and and_6 (and_6_out, in_1[5], xor_1_out[5]);
  xor xor_7 (xor_7_out, in_1[6], xor_1_out[6]);
  and and_7 (and_7_out, in_1[6], xor_1_out[6]);
  xor xor_8 (xor_8_out, in_1[7], xor_1_out[7]);
  and and_8 (and_8_out, in_1[7], xor_1_out[7]);
  xor xor_9 (xor_9_out, in_1[4], xor_1_out[4]);
  xor xor_10 (xor_10_out, in_1[8], xor_1_out[8]);
  and and_9 (and_9_out, in_1[8], xor_1_out[8]);
  xor xor_11 (xor_11_out, in_1[9], xor_1_out[9]);
  and and_10 (and_10_out, in_1[9], xor_1_out[9]);
  xor xor_12 (xor_12_out, in_1[10], xor_1_out[10]);
  and and_11 (and_11_out, in_1[10], xor_1_out[10]);
  xor xor_13 (xor_13_out, in_1[11], xor_1_out[11]);
  and and_12 (and_12_out, in_1[11], xor_1_out[11]);
  xor xor_14 (xor_14_out, in_1[13], xor_1_out[13]);
  and and_13 (and_13_out, in_1[13], xor_1_out[13]);
  xor xor_15 (xor_15_out, in_1[14], xor_1_out[14]);
  and and_14 (and_14_out, in_1[14], xor_1_out[14]);
  xor xor_16 (xor_16_out, in_1[15], xor_1_out[15]);
  and and_15 (and_15_out, in_1[15], xor_1_out[15]);
  xor xor_17 (xor_17_out, in_1[12], xor_1_out[12]);
  and and_16 (and_16_out, in_1[12], xor_1_out[12]);
  xor xor_18 (xor_18_out[0], xor_2_out, in_2);
  xor xor_19 (xor_18_out[1], xor_3_out, or_1_out);
  and and_17 (and_17_out, xor_2_out, in_2);
  xor xor_20 (xor_18_out[2], xor_4_out, or_4_out);
  and and_18 (and_18_out, xor_2_out, xor_3_out, in_2);
  and and_19 (and_19_out, xor_3_out, and_1_out);
  xor xor_21 (xor_18_out[3], xor_5_out, or_2_out);
  and and_20 (and_20_out, xor_4_out, xor_3_out, and_1_out);
  and and_21 (and_21_out, xor_4_out, xor_3_out, xor_2_out, in_2);
  and and_22 (and_22_out, xor_4_out, and_2_out);
  and and_23 (and_23_out, xor_5_out, and_3_out);
  and and_24 (and_24_out, xor_5_out, xor_4_out, xor_3_out, and_1_out);
  and and_25 (and_25_out, xor_5_out, xor_4_out, xor_3_out, xor_2_out, in_2);
  and and_26 (and_26_out, xor_5_out, xor_4_out, and_2_out);
  xor xor_22 (xor_18_out[4], xor_9_out, or_9_out);
  xor xor_23 (xor_18_out[5], xor_6_out, or_3_out);
  and and_27 (and_27_out, xor_9_out, or_9_out);
  and and_28 (and_28_out, xor_9_out, xor_6_out, or_9_out);
  and and_29 (and_29_out, xor_6_out, and_5_out);
  and and_30 (and_30_out, xor_7_out, xor_6_out, and_5_out);
  and and_31 (and_31_out, xor_7_out, xor_6_out, xor_9_out, or_9_out);
  and and_32 (and_32_out, xor_7_out, and_6_out);
  and and_33 (and_33_out, xor_8_out, xor_7_out, xor_6_out, xor_9_out, or_9_out);
  and and_34 (and_34_out, xor_8_out, xor_7_out, and_6_out);
  or or_1 (or_1_out, and_17_out, and_1_out);
  or or_2 (or_2_out, and_3_out, and_20_out, and_21_out, and_22_out);
  or or_3 (or_3_out, and_27_out, and_5_out);
  xor xor_24 (xor_18_out[6], xor_7_out, or_5_out);
  xor xor_25 (xor_18_out[7], xor_8_out, or_6_out);
  and and_35 (and_35_out, xor_8_out, and_7_out);
  and and_36 (and_36_out, xor_8_out, xor_7_out, xor_6_out, and_5_out);
  xor xor_26 (xor_18_out[8], xor_10_out, or_10_out);
  xor xor_27 (xor_18_out[9], xor_11_out, or_7_out);
  and and_37 (and_37_out, xor_10_out, or_10_out);
  xor xor_28 (xor_18_out[10], xor_12_out, or_11_out);
  and and_38 (and_38_out, xor_10_out, xor_11_out, or_10_out);
  and and_39 (and_39_out, xor_11_out, and_9_out);
  xor xor_29 (xor_18_out[11], xor_13_out, or_12_out);
  and and_40 (and_40_out, xor_12_out, xor_11_out, and_9_out);
  and and_41 (and_41_out, xor_12_out, xor_11_out, xor_10_out, or_10_out);
  and and_42 (and_42_out, xor_12_out, and_10_out);
  and and_43 (and_43_out, xor_13_out, xor_12_out, xor_11_out, xor_10_out, or_10_out);
  and and_44 (and_44_out, xor_13_out, xor_12_out, and_10_out);
  xor xor_30 (xor_18_out[12], xor_17_out, or_15_out);
  and and_45 (and_45_out, xor_17_out, or_15_out);
  and and_46 (and_46_out, xor_14_out, and_16_out);
  and and_47 (and_47_out, xor_15_out, xor_14_out, and_16_out);
  and and_48 (and_48_out, xor_15_out, xor_14_out, xor_17_out, or_15_out);
  and and_49 (and_49_out, xor_15_out, and_13_out);
  or or_4 (or_4_out, and_18_out, and_19_out, and_2_out);
  or or_5 (or_5_out, and_28_out, and_29_out, and_6_out);
  or or_6 (or_6_out, and_7_out, and_30_out, and_31_out, and_32_out);
  or or_7 (or_7_out, and_37_out, and_9_out);
  and and_50 (and_50_out, xor_13_out, and_11_out);
  and and_51 (and_51_out, xor_13_out, xor_12_out, xor_11_out, and_9_out);
  xor xor_31 (xor_18_out[13], xor_14_out, or_8_out);
  or or_8 (or_8_out, and_45_out, and_16_out);
  xor xor_32 (xor_18_out[14], xor_15_out, or_13_out);
  and and_52 (and_52_out, xor_17_out, xor_14_out, or_15_out);
  xor xor_33 (xor_18_out[15], xor_16_out, or_14_out);
  and and_53 (and_53_out, xor_16_out, and_14_out);
  and and_54 (and_54_out, xor_16_out, xor_15_out, xor_14_out, and_16_out);
  and and_55 (and_55_out, xor_16_out, xor_15_out, xor_14_out, xor_17_out, or_15_out);
  and and_56 (and_56_out, xor_16_out, xor_15_out, and_13_out);
  or or_9 (or_9_out, and_4_out, and_23_out, and_24_out, and_25_out, and_26_out);
  or or_10 (or_10_out, and_8_out, and_35_out, and_36_out, and_33_out, and_34_out);
  or or_11 (or_11_out, and_38_out, and_39_out, and_10_out);
  or or_12 (or_12_out, and_11_out, and_40_out, and_41_out, and_42_out);
  or or_13 (or_13_out, and_52_out, and_46_out, and_13_out);
  or or_14 (or_14_out, and_14_out, and_47_out, and_48_out, and_49_out);
  or or_15 (or_15_out, and_12_out, and_50_out, and_51_out, and_43_out, and_44_out);
  or or_16 (out_8, and_15_out, and_53_out, and_54_out, and_55_out, and_56_out);
  not not_1 (not_1_out, xor_18_out[8]);
  and and_57 (out_6, not_1_out, in_2);
  Multiplexer #(.width(16)) multiplexer_1 (
    .in0(xor_18_out), .in1({{8{in_3}}, fa_1_out_4}), .out(out_7), .sel(out_6));  // open: en
  not not_2 (not_2_out, in_2);
  not not_3 (not_3_out, xor_18_out[0]);
  not not_4 (not_4_out, xor_18_out[1]);
  not not_5 (not_5_out, xor_18_out[2]);
  not not_6 (not_6_out, xor_18_out[3]);
  not not_7 (not_7_out, xor_18_out[4]);
  not not_8 (not_8_out, xor_18_out[5]);
  not not_9 (not_9_out, xor_18_out[6]);
  not not_10 (not_10_out, xor_18_out[7]);
  FA fa_1 (.in_1(not_3_out), .in_2(in_2), .in_3(not_2_out), .out_4(fa_1_out_4[0]), .out_5(fa_1_out_5));
  FA fa_2 (.in_1(not_4_out), .in_2(not_2_out), .in_3(fa_1_out_5), .out_4(fa_1_out_4[1]), .out_5(fa_2_out_5));
  FA fa_3 (.in_1(not_5_out), .in_2(not_2_out), .in_3(fa_2_out_5), .out_4(fa_1_out_4[2]), .out_5(fa_3_out_5));
  FA fa_4 (.in_1(not_6_out), .in_2(not_2_out), .in_3(fa_3_out_5), .out_4(fa_1_out_4[3]), .out_5(fa_4_out_5));
  FA fa_5 (.in_1(not_7_out), .in_2(not_2_out), .in_3(fa_4_out_5), .out_4(fa_1_out_4[4]), .out_5(fa_5_out_5));
  FA fa_6 (.in_1(not_8_out), .in_2(not_2_out), .in_3(fa_5_out_5), .out_4(fa_1_out_4[5]), .out_5(fa_6_out_5));
  FA fa_7 (.in_1(not_9_out), .in_2(not_2_out), .in_3(fa_6_out_5), .out_4(fa_1_out_4[6]), .out_5(fa_7_out_5));
  FA fa_8 (.in_1(not_10_out), .in_2(not_2_out), .in_3(fa_7_out_5), .out_4(fa_1_out_4[7]));  // open: out_5

  // Other names for the same wires on the sheet: c = in_2

  // Notes on the sheet:
  //   C1
  //   G1
  //   G2
  //   G3
  //   G4
  //   C1
  //   C1
  //   P1
  //   P2
  //   P3
  //   P4
  //   P1
  //   G1
  //   P2
  //   G2
  //   P3
  //   G3
  //   P4
  //   G4
  //   G1
  //   G3
  //   G4
  //   C1
  //   P1
  //   P2
  //   G2
  //   P3
  //   P4
  //   P1
  //   G1
  //   P2
  //   G2
  //   P3
  //   G3
  //   P4
  //   G4
endmodule

module multiplier (
  input  [7:0] in_1,
  input  [7:0] in_2,
  input  in_3,
  input  in_4,
  input  in_5,
  input  in_6,
  input  in_7,
  input  in_8,
  input  in_9,
  input  in_10,
  input  in_11,
  input  in_12,
  input  in_13,
  input  in_14,
  input  in_15,
  input  in_16,
  input  in_17,
  input  in_18,
  input  in_19,
  input  in_20,
  input  in_21,
  input  in_22,
  input  in_23,
  input  in_24,
  input  in_25,
  input  in_26,
  input  in_27,
  input  in_28,
  input  in_29,
  input  in_30,
  input  in_31,
  input  in_32,
  input  in_33,
  input  in_34,
  input  in_35,
  input  in_36,
  input  in_37,
  input  in_38,
  input  in_39,
  input  in_40,
  input  in_41,
  input  in_42,
  input  in_43,
  input  in_44,
  input  in_45,
  input  in_46,
  input  in_47,
  input  in_48,
  input  in_49,
  input  in_50,
  input  in_51,
  input  in_52,
  input  in_53,
  input  in_54,
  input  in_55,
  input  in_56,
  input  in_57,
  input  in_58,
  input  in_59,
  input  in_60,
  input  in_61,
  input  in_62,
  input  in_63,
  input  in_64,
  input  in_65,
  input  in_66,
  input  in_67,
  input  in_68,
  input  in_69,
  input  in_70,
  input  in_71,
  input  in_72,
  input  in_73,
  input  in_74,
  input  in_75,
  input  in_76,
  input  in_77,
  input  in_78,
  input  in_79,
  input  in_80,
  input  in_81,
  input  in_82,
  input  in_83,
  input  in_84,
  input  in_85,
  input  in_86,
  input  in_87,
  input  in_88,
  input  in_89,
  input  in_90,
  input  in_91,
  input  in_92,
  input  in_93,
  input  in_94,
  input  in_95,
  output [15:0] out_96
);

  wire [7:0] multiplexer_1_out;
  wire [8:1] multiplexer_9_out;
  wire [9:2] multiplexer_17_out;
  wire [10:3] multiplexer_25_out;
  wire [11:4] multiplexer_33_out;
  wire [12:5] multiplexer_41_out;
  wire [13:6] multiplexer_49_out;
  wire [14:7] multiplexer_57_out;
  wire [15:0] n16bitadder_1_out_7, n16bitadder_2_out_7, n16bitadder_3_out_7, n16bitadder_4_out_7,
       n16bitadder_5_out_7, n16bitadder_6_out_7;

  Multiplexer multiplexer_1 (.in0(in_3), .in1(in_2[0]), .out(multiplexer_1_out[0]), .sel(in_1[0]));  // open: en
  Multiplexer multiplexer_2 (.in0(in_4), .in1(in_2[1]), .out(multiplexer_1_out[1]), .sel(in_1[0]));  // open: en
  Multiplexer multiplexer_3 (.in0(in_6), .in1(in_2[2]), .out(multiplexer_1_out[2]), .sel(in_1[0]));  // open: en
  Multiplexer multiplexer_4 (.in0(in_13), .in1(in_2[3]), .out(multiplexer_1_out[3]), .sel(in_1[0]));  // open: en
  Multiplexer multiplexer_5 (.in0(in_21), .in1(in_2[4]), .out(multiplexer_1_out[4]), .sel(in_1[0]));  // open: en
  Multiplexer multiplexer_6 (.in0(in_28), .in1(in_2[5]), .out(multiplexer_1_out[5]), .sel(in_1[0]));  // open: en
  Multiplexer multiplexer_7 (.in0(in_31), .in1(in_2[6]), .out(multiplexer_1_out[6]), .sel(in_1[0]));  // open: en
  Multiplexer multiplexer_8 (.in0(in_32), .in1(in_2[7]), .out(multiplexer_1_out[7]), .sel(in_1[0]));  // open: en
  Multiplexer multiplexer_9 (.in0(in_33), .in1(in_2[0]), .out(multiplexer_9_out[1]), .sel(in_1[1]));  // open: en
  Multiplexer multiplexer_10 (.in0(in_34), .in1(in_2[1]), .out(multiplexer_9_out[2]), .sel(in_1[1]));  // open: en
  Multiplexer multiplexer_11 (.in0(in_35), .in1(in_2[2]), .out(multiplexer_9_out[3]), .sel(in_1[1]));  // open: en
  Multiplexer multiplexer_12 (.in0(in_37), .in1(in_2[3]), .out(multiplexer_9_out[4]), .sel(in_1[1]));  // open: en
  Multiplexer multiplexer_13 (.in0(in_38), .in1(in_2[4]), .out(multiplexer_9_out[5]), .sel(in_1[1]));  // open: en
  Multiplexer multiplexer_14 (.in0(in_39), .in1(in_2[5]), .out(multiplexer_9_out[6]), .sel(in_1[1]));  // open: en
  Multiplexer multiplexer_15 (.in0(in_40), .in1(in_2[6]), .out(multiplexer_9_out[7]), .sel(in_1[1]));  // open: en
  Multiplexer multiplexer_16 (.in0(in_41), .in1(in_2[7]), .out(multiplexer_9_out[8]), .sel(in_1[1]));  // open: en
  Multiplexer multiplexer_17 (.in0(in_42), .in1(in_2[0]), .out(multiplexer_17_out[2]), .sel(in_1[2]));  // open: en
  Multiplexer multiplexer_18 (.in0(in_43), .in1(in_2[1]), .out(multiplexer_17_out[3]), .sel(in_1[2]));  // open: en
  Multiplexer multiplexer_19 (.in0(in_45), .in1(in_2[2]), .out(multiplexer_17_out[4]), .sel(in_1[2]));  // open: en
  Multiplexer multiplexer_20 (.in0(in_46), .in1(in_2[3]), .out(multiplexer_17_out[5]), .sel(in_1[2]));  // open: en
  Multiplexer multiplexer_21 (.in0(in_47), .in1(in_2[4]), .out(multiplexer_17_out[6]), .sel(in_1[2]));  // open: en
  Multiplexer multiplexer_22 (.in0(in_48), .in1(in_2[5]), .out(multiplexer_17_out[7]), .sel(in_1[2]));  // open: en
  Multiplexer multiplexer_23 (.in0(in_49), .in1(in_2[6]), .out(multiplexer_17_out[8]), .sel(in_1[2]));  // open: en
  Multiplexer multiplexer_24 (.in0(in_50), .in1(in_2[7]), .out(multiplexer_17_out[9]), .sel(in_1[2]));  // open: en
  Multiplexer multiplexer_25 (.in0(in_51), .in1(in_2[0]), .out(multiplexer_25_out[3]), .sel(in_1[3]));  // open: en
  Multiplexer multiplexer_26 (.in0(in_52), .in1(in_2[1]), .out(multiplexer_25_out[4]), .sel(in_1[3]));  // open: en
  Multiplexer multiplexer_27 (.in0(in_54), .in1(in_2[2]), .out(multiplexer_25_out[5]), .sel(in_1[3]));  // open: en
  Multiplexer multiplexer_28 (.in0(in_55), .in1(in_2[3]), .out(multiplexer_25_out[6]), .sel(in_1[3]));  // open: en
  Multiplexer multiplexer_29 (.in0(in_56), .in1(in_2[4]), .out(multiplexer_25_out[7]), .sel(in_1[3]));  // open: en
  Multiplexer multiplexer_30 (.in0(in_57), .in1(in_2[5]), .out(multiplexer_25_out[8]), .sel(in_1[3]));  // open: en
  Multiplexer multiplexer_31 (.in0(in_58), .in1(in_2[6]), .out(multiplexer_25_out[9]), .sel(in_1[3]));  // open: en
  Multiplexer multiplexer_32 (.in0(in_59), .in1(in_2[7]), .out(multiplexer_25_out[10]), .sel(in_1[3]));  // open: en
  Multiplexer multiplexer_33 (.in0(in_60), .in1(in_2[0]), .out(multiplexer_33_out[4]), .sel(in_1[4]));  // open: en
  Multiplexer multiplexer_34 (.in0(in_61), .in1(in_2[1]), .out(multiplexer_33_out[5]), .sel(in_1[4]));  // open: en
  Multiplexer multiplexer_35 (.in0(in_62), .in1(in_2[2]), .out(multiplexer_33_out[6]), .sel(in_1[4]));  // open: en
  Multiplexer multiplexer_36 (.in0(in_64), .in1(in_2[3]), .out(multiplexer_33_out[7]), .sel(in_1[4]));  // open: en
  Multiplexer multiplexer_37 (.in0(in_65), .in1(in_2[4]), .out(multiplexer_33_out[8]), .sel(in_1[4]));  // open: en
  Multiplexer multiplexer_38 (.in0(in_66), .in1(in_2[5]), .out(multiplexer_33_out[9]), .sel(in_1[4]));  // open: en
  Multiplexer multiplexer_39 (.in0(in_67), .in1(in_2[6]), .out(multiplexer_33_out[10]), .sel(in_1[4]));  // open: en
  Multiplexer multiplexer_40 (.in0(in_68), .in1(in_2[7]), .out(multiplexer_33_out[11]), .sel(in_1[4]));  // open: en
  Multiplexer multiplexer_41 (.in0(in_69), .in1(in_2[0]), .out(multiplexer_41_out[5]), .sel(in_1[5]));  // open: en
  Multiplexer multiplexer_42 (.in0(in_70), .in1(in_2[1]), .out(multiplexer_41_out[6]), .sel(in_1[5]));  // open: en
  Multiplexer multiplexer_43 (.in0(in_72), .in1(in_2[2]), .out(multiplexer_41_out[7]), .sel(in_1[5]));  // open: en
  Multiplexer multiplexer_44 (.in0(in_73), .in1(in_2[3]), .out(multiplexer_41_out[8]), .sel(in_1[5]));  // open: en
  Multiplexer multiplexer_45 (.in0(in_74), .in1(in_2[4]), .out(multiplexer_41_out[9]), .sel(in_1[5]));  // open: en
  Multiplexer multiplexer_46 (.in0(in_75), .in1(in_2[5]), .out(multiplexer_41_out[10]), .sel(in_1[5]));  // open: en
  Multiplexer multiplexer_47 (.in0(in_76), .in1(in_2[6]), .out(multiplexer_41_out[11]), .sel(in_1[5]));  // open: en
  Multiplexer multiplexer_48 (.in0(in_77), .in1(in_2[7]), .out(multiplexer_41_out[12]), .sel(in_1[5]));  // open: en
  Multiplexer multiplexer_49 (.in0(in_78), .in1(in_2[0]), .out(multiplexer_49_out[6]), .sel(in_1[6]));  // open: en
  Multiplexer multiplexer_50 (.in0(in_79), .in1(in_2[1]), .out(multiplexer_49_out[7]), .sel(in_1[6]));  // open: en
  Multiplexer multiplexer_51 (.in0(in_80), .in1(in_2[2]), .out(multiplexer_49_out[8]), .sel(in_1[6]));  // open: en
  Multiplexer multiplexer_52 (.in0(in_82), .in1(in_2[3]), .out(multiplexer_49_out[9]), .sel(in_1[6]));  // open: en
  Multiplexer multiplexer_53 (.in0(in_83), .in1(in_2[4]), .out(multiplexer_49_out[10]), .sel(in_1[6]));  // open: en
  Multiplexer multiplexer_54 (.in0(in_84), .in1(in_2[5]), .out(multiplexer_49_out[11]), .sel(in_1[6]));  // open: en
  Multiplexer multiplexer_55 (.in0(in_85), .in1(in_2[6]), .out(multiplexer_49_out[12]), .sel(in_1[6]));  // open: en
  Multiplexer multiplexer_56 (.in0(in_86), .in1(in_2[7]), .out(multiplexer_49_out[13]), .sel(in_1[6]));  // open: en
  Multiplexer multiplexer_57 (.in0(in_87), .in1(in_2[0]), .out(multiplexer_57_out[7]), .sel(in_1[7]));  // open: en
  Multiplexer multiplexer_58 (.in0(in_88), .in1(in_2[1]), .out(multiplexer_57_out[8]), .sel(in_1[7]));  // open: en
  Multiplexer multiplexer_59 (.in0(in_89), .in1(in_2[2]), .out(multiplexer_57_out[9]), .sel(in_1[7]));  // open: en
  Multiplexer multiplexer_60 (.in0(in_91), .in1(in_2[3]), .out(multiplexer_57_out[10]), .sel(in_1[7]));  // open: en
  Multiplexer multiplexer_61 (.in0(in_92), .in1(in_2[4]), .out(multiplexer_57_out[11]), .sel(in_1[7]));  // open: en
  Multiplexer multiplexer_62 (.in0(in_93), .in1(in_2[5]), .out(multiplexer_57_out[12]), .sel(in_1[7]));  // open: en
  Multiplexer multiplexer_63 (.in0(in_94), .in1(in_2[6]), .out(multiplexer_57_out[13]), .sel(in_1[7]));  // open: en
  Multiplexer multiplexer_64 (.in0(in_95), .in1(in_2[7]), .out(multiplexer_57_out[14]), .sel(in_1[7]));  // open: en
  _16bitadder u_16bitadder_1 (
    .in_1({{8{in_17}}, multiplexer_1_out}), .in_4({{7{in_36}}, multiplexer_9_out, in_36}), .in_2(in_5),
    .in_3(in_9), .out_7(n16bitadder_1_out_7), .in_5(in_8));  // open: out_8, out_6
  _16bitadder u_16bitadder_2 (
    .in_1({{6{in_44}}, multiplexer_17_out, {2{in_44}}}), .in_4({{5{in_53}}, multiplexer_25_out, {3{in_53}}}),
    .in_2(in_12), .in_3(in_15), .out_7(n16bitadder_2_out_7), .in_5(in_14));  // open: out_8, out_6
  _16bitadder u_16bitadder_3 (
    .in_1(n16bitadder_1_out_7), .in_4(n16bitadder_2_out_7), .in_2(in_7), .in_3(in_11),
    .out_7(n16bitadder_3_out_7), .in_5(in_10));  // open: out_8, out_6
  _16bitadder u_16bitadder_4 (
    .in_1({{3{in_71}}, multiplexer_41_out, {5{in_71}}}), .in_4({{4{in_63}}, multiplexer_33_out, {4{in_63}}}),
    .in_2(in_20), .in_3(in_25), .out_7(n16bitadder_4_out_7), .in_5(in_23));  // open: out_8, out_6
  _16bitadder u_16bitadder_5 (
    .in_1({in_90, multiplexer_57_out, {7{in_90}}}), .in_4({{2{in_81}}, multiplexer_49_out, {6{in_81}}}),
    .in_2(in_27), .in_3(in_30), .out_7(n16bitadder_5_out_7), .in_5(in_29));  // open: out_8, out_6
  _16bitadder u_16bitadder_6 (
    .in_1(n16bitadder_5_out_7), .in_4(n16bitadder_4_out_7), .in_2(in_22), .in_3(in_24),
    .out_7(n16bitadder_6_out_7), .in_5(in_26));  // open: out_8, out_6
  _16bitadder u_16bitadder_7 (
    .in_1(n16bitadder_6_out_7), .in_4(n16bitadder_3_out_7), .in_2(in_16), .in_3(in_19), .out_7(out_96),
    .in_5(in_18));  // open: out_8, out_6
endmodule

module _1bit_16 (
  input  in_1,
  input  [15:0] in_2,
  input  [15:0] in_3,
  output [15:0] out_4
);

  wire fa_1_out_5, fa_2_out_5, fa_3_out_5, fa_4_out_5, fa_5_out_5, fa_6_out_5, fa_7_out_5, fa_8_out_5,
       fa_9_out_5, fa_10_out_5, fa_11_out_5, fa_12_out_5, fa_13_out_5, fa_14_out_5, fa_15_out_5, fa_16_out_5;
  wire [15:0] xor_1_out;

  assign xor_1_out = in_3 ^ {16{in_1}};  // XOR_Gate xor_1, 16 bits wide
  FA fa_1 (.in_1(in_2[0]), .in_2(xor_1_out[0]), .in_3(in_1), .out_4(out_4[0]), .out_5(fa_1_out_5));
  FA fa_2 (.in_1(in_2[1]), .in_2(xor_1_out[1]), .in_3(fa_1_out_5), .out_4(out_4[1]), .out_5(fa_2_out_5));
  FA fa_3 (.in_1(in_2[2]), .in_2(xor_1_out[2]), .in_3(fa_2_out_5), .out_4(out_4[2]), .out_5(fa_3_out_5));
  FA fa_4 (.in_1(in_2[3]), .in_2(xor_1_out[3]), .in_3(fa_3_out_5), .out_4(out_4[3]), .out_5(fa_4_out_5));
  FA fa_5 (.in_1(in_2[4]), .in_2(xor_1_out[4]), .in_3(fa_4_out_5), .out_4(out_4[4]), .out_5(fa_5_out_5));
  FA fa_6 (.in_1(in_2[5]), .in_2(xor_1_out[5]), .in_3(fa_5_out_5), .out_4(out_4[5]), .out_5(fa_6_out_5));
  FA fa_7 (.in_1(in_2[6]), .in_2(xor_1_out[6]), .in_3(fa_6_out_5), .out_4(out_4[6]), .out_5(fa_7_out_5));
  FA fa_8 (.in_1(in_2[7]), .in_2(xor_1_out[7]), .in_3(fa_7_out_5), .out_4(out_4[7]), .out_5(fa_8_out_5));
  FA fa_9 (.in_1(in_2[8]), .in_2(xor_1_out[8]), .in_3(fa_8_out_5), .out_4(out_4[8]), .out_5(fa_9_out_5));
  FA fa_10 (.in_1(in_2[9]), .in_2(xor_1_out[9]), .in_3(fa_9_out_5), .out_4(out_4[9]), .out_5(fa_10_out_5));
  FA fa_11 (.in_1(in_2[10]), .in_2(xor_1_out[10]), .in_3(fa_10_out_5), .out_4(out_4[10]), .out_5(fa_11_out_5));
  FA fa_12 (.in_1(in_2[11]), .in_2(xor_1_out[11]), .in_3(fa_11_out_5), .out_4(out_4[11]), .out_5(fa_12_out_5));
  FA fa_13 (.in_1(in_2[12]), .in_2(xor_1_out[12]), .in_3(fa_12_out_5), .out_4(out_4[12]), .out_5(fa_13_out_5));
  FA fa_14 (.in_1(in_2[13]), .in_2(xor_1_out[13]), .in_3(fa_13_out_5), .out_4(out_4[13]), .out_5(fa_14_out_5));
  FA fa_15 (.in_1(in_2[14]), .in_2(xor_1_out[14]), .in_3(fa_14_out_5), .out_4(out_4[14]), .out_5(fa_15_out_5));
  FA fa_16 (.in_1(in_2[15]), .in_2(xor_1_out[15]), .in_3(fa_15_out_5), .out_4(out_4[15]), .out_5(fa_16_out_5));

  // Other names for the same wires on the sheet: C = in_1
endmodule

// Q4
module calc (
  input  in_1,
  input  in_2,
  input  in_3,
  input  in_4,
  input  in_5,
  input  in_6,
  input  in_7,
  input  in_8,
  input  in_9,
  input  in_10,
  input  in_11,
  input  in_12,
  input  in_13,
  input  in_14,
  input  in_15,
  input  in_16,
  input  [1:0] in_17,
  input  in_18,
  input  Adder,
  input  Subtracter,
  input  in_21,
  input  in_22,
  input  in_23,
  input  in_24,
  input  in_25,
  input  in_26,
  input  in_27,
  input  in_28,
  input  in_29,
  input  in_30,
  input  in_31,
  input  in_32
);

  wire _71, _72, _73, _74, _75, _76, _77, _78, _79, _80, _81, _82, _83, _84, _85, _86, FLAG, n7sd_1_a,
       n7sd_1_b_2, n7sd_1_c_2, n7sd_1_d_2, n7sd_1_e, n7sd_1_f, n7sd_1_g, n7sd_2_a, n7sd_2_b_2, n7sd_2_c_2,
       n7sd_2_d_2, n7sd_2_e, n7sd_2_f, n7sd_2_g, n7sd_3_a, n7sd_3_b_2, n7sd_3_c_2, n7sd_3_d_2, n7sd_3_e,
       n7sd_3_f, n7sd_3_g, n7sd_4_a, n7sd_4_b_2, n7sd_4_c_2, n7sd_4_d_2, n7sd_4_e, n7sd_4_f, n7sd_4_g,
       n7sd_5_a, n7sd_5_b_2, n7sd_5_c_2, n7sd_5_d_2, n7sd_5_e, n7sd_5_f, n7sd_5_g, n7sd_6_a, n7sd_6_b_2,
       n7sd_6_c_2, n7sd_6_d_2, n7sd_6_e, n7sd_6_f, n7sd_6_g, n7sd_7_a, n7sd_7_b_2, n7sd_7_c_2, n7sd_7_d_2,
       n7sd_7_e, n7sd_7_f, n7sd_7_g, n7sd_8_a, n7sd_8_b_2, n7sd_8_c_2, n7sd_8_d_2, n7sd_8_e, n7sd_8_f,
       n7sd_8_g, Q0, Q1, Q2, Q3, Q4, Q5, Q6, Q7, R0, R1, R2, R3, R4, R5, R6, R7;
  wire [15:0] ADD, MUL, SUB;

  _16bitadder u_16bitadder_1 (
    .in_1({{8{in_25}}, in_1, in_2, in_3, in_4, in_5, in_6, in_7, in_8}),
    .in_4({{8{in_28}}, in_9, in_10, in_11, in_12, in_13, in_14, in_15, in_16}), .in_2(Adder), .in_3(in_21),
    .out_7(ADD), .in_5(in_24));  // open: out_8, out_6
  Multiplexer #(.select(2), .width(16)) multiplexer_1 (
    .in0(ADD), .in1(SUB), .in2(MUL),
    .out({_86, _85, _84, _83, _82, _81, _80, _79, _78, _77, _76, _75, _74, _73, _72, _71}), .sel(in_17));  // open: in3, en
  _16bitadder u_16bitadder_2 (
    .in_1({{8{in_29}}, in_9, in_10, in_11, in_12, in_13, in_14, in_15, in_16}),
    .in_4({{8{in_26}}, in_1, in_2, in_3, in_4, in_5, in_6, in_7, in_8}), .in_2(Subtracter), .in_3(in_23),
    .out_7(SUB), .out_6(FLAG), .in_5(in_22));  // open: out_8
  multiplier multiplier_1 (
    .in_3(in_31), .in_4(in_31), .in_6(in_31), .in_9(in_31), .in_13(in_31), .in_17(in_31), .in_19(in_31),
    .in_21(in_31), .in_24(in_31), .in_25(in_31), .in_28(in_31), .in_30(in_31), .in_31(in_31), .in_32(in_31),
    .in_33(in_31), .in_34(in_31), .in_35(in_31), .in_36(in_31), .in_37(in_31), .in_38(in_31), .in_39(in_31),
    .in_40(in_31), .in_41(in_31), .in_42(in_31), .in_43(in_31), .in_45(in_31), .in_46(in_31), .in_47(in_31),
    .in_48(in_31), .in_49(in_31), .in_50(in_31), .in_51(in_31), .in_52(in_31), .in_54(in_31), .in_55(in_31),
    .in_56(in_31), .in_57(in_31), .in_58(in_31), .in_59(in_31), .in_60(in_31), .in_61(in_31), .in_62(in_31),
    .in_64(in_31), .in_65(in_31), .in_66(in_31), .in_67(in_31), .in_68(in_31), .in_69(in_31), .in_70(in_31),
    .in_72(in_31), .in_73(in_31), .in_74(in_31), .in_75(in_31), .in_76(in_31), .in_77(in_31), .in_78(in_31),
    .in_79(in_31), .in_80(in_31), .in_82(in_31), .in_83(in_31), .in_84(in_31), .in_85(in_31), .in_86(in_31),
    .in_87(in_31), .in_88(in_31), .in_89(in_31), .in_91(in_31), .in_92(in_31), .in_93(in_31), .in_94(in_31),
    .in_95(in_31), .in_63(in_18), .in_71(in_18), .in_81(in_18), .in_53(in_18), .in_90(in_18), .in_44(in_18),
    .in_5(in_18), .in_12(in_18), .in_7(in_18), .in_20(in_18), .in_27(in_18), .in_22(in_18), .in_16(in_18),
    .in_8(in_32), .in_15(in_32), .in_14(in_32), .in_11(in_32), .in_10(in_32), .in_23(in_32), .in_29(in_32),
    .in_26(in_32), .in_18(in_32), .in_1({in_1, in_2, in_3, in_4, in_5, in_6, in_7, in_8}),
    .in_2({in_9, in_10, in_11, in_12, in_13, in_14, in_15, in_16}), .out_96(MUL));
  _7_Segment_Display u_7_segment_display_1 (.g(FLAG));  // open: f, a, b, e, d, c, dp
  _7SD u_7sd_1 (
    .in_1(_86), .B(_85), .C(_84), .D(_83), .a(n7sd_1_a), .b_2(n7sd_1_b_2), .c_2(n7sd_1_c_2),
    .d_2(n7sd_1_d_2), .e(n7sd_1_e), .f(n7sd_1_f), .g(n7sd_1_g));
  _7_Segment_Display u_7_segment_display_2 (
    .g(n7sd_1_g), .f(n7sd_1_f), .a(n7sd_1_a), .b(n7sd_1_b_2), .e(n7sd_1_e), .d(n7sd_1_d_2), .c(n7sd_1_c_2));  // open: dp
  _7SD u_7sd_2 (
    .in_1(_78), .B(_77), .C(_76), .D(_75), .a(n7sd_2_a), .b_2(n7sd_2_b_2), .c_2(n7sd_2_c_2),
    .d_2(n7sd_2_d_2), .e(n7sd_2_e), .f(n7sd_2_f), .g(n7sd_2_g));
  _7_Segment_Display u_7_segment_display_3 (
    .g(n7sd_3_g), .f(n7sd_3_f), .a(n7sd_3_a), .b(n7sd_3_b_2), .e(n7sd_3_e), .d(n7sd_3_d_2), .c(n7sd_3_c_2));  // open: dp
  _7_Segment_Display u_7_segment_display_4 (
    .g(n7sd_2_g), .f(n7sd_2_f), .a(n7sd_2_a), .b(n7sd_2_b_2), .e(n7sd_2_e), .d(n7sd_2_d_2), .c(n7sd_2_c_2));  // open: dp
  _7SD u_7sd_3 (
    .in_1(_82), .B(_81), .C(_80), .D(_79), .a(n7sd_3_a), .b_2(n7sd_3_b_2), .c_2(n7sd_3_c_2),
    .d_2(n7sd_3_d_2), .e(n7sd_3_e), .f(n7sd_3_f), .g(n7sd_3_g));
  _7_Segment_Display u_7_segment_display_5 (
    .g(n7sd_4_g), .f(n7sd_4_f), .a(n7sd_4_a), .b(n7sd_4_b_2), .e(n7sd_4_e), .d(n7sd_4_d_2), .c(n7sd_4_c_2));  // open: dp
  _7SD u_7sd_4 (
    .in_1(_74), .B(_73), .C(_72), .D(_71), .a(n7sd_4_a), .b_2(n7sd_4_b_2), .c_2(n7sd_4_c_2),
    .d_2(n7sd_4_d_2), .e(n7sd_4_e), .f(n7sd_4_f), .g(n7sd_4_g));
  _8_bit_div u_8_bit_div_1 (
    .in_17(in_27), .out_26(Q7), .out_27(Q6), .out_28(Q5), .out_29(Q4), .out_30(Q3), .out_31(Q2), .out_32(Q1),
    .out_33(Q0), .in_1(in_1), .in_2(in_2), .in_3(in_3), .in_4(in_4), .in_5(in_5), .in_6(in_6), .in_7(in_7),
    .in_8(in_8), .in_9(in_9), .in_10(in_10), .in_11(in_11), .in_12(in_12), .in_13(in_13), .in_14(in_14),
    .in_15(in_15), .in_16(in_16), .out_34(R7), .out_35(R6), .out_36(R5), .out_37(R4), .out_38(R3),
    .out_39(R2), .out_40(R1), .out_41(R0), .in_18(in_30), .in_19(in_30), .in_20(in_30), .in_21(in_30),
    .in_22(in_30), .in_23(in_30), .in_24(in_30), .in_25(in_30));
  _7SD u_7sd_5 (
    .in_1(Q7), .B(Q6), .C(Q5), .D(Q4), .a(n7sd_5_a), .b_2(n7sd_5_b_2), .c_2(n7sd_5_c_2), .d_2(n7sd_5_d_2),
    .e(n7sd_5_e), .f(n7sd_5_f), .g(n7sd_5_g));
  _7SD u_7sd_6 (
    .in_1(R7), .B(R6), .C(R5), .D(R4), .a(n7sd_6_a), .b_2(n7sd_6_b_2), .c_2(n7sd_6_c_2), .d_2(n7sd_6_d_2),
    .e(n7sd_6_e), .f(n7sd_6_f), .g(n7sd_6_g));
  _7_Segment_Display u_7_segment_display_6 (
    .g(n7sd_5_g), .f(n7sd_5_f), .a(n7sd_5_a), .b(n7sd_5_b_2), .e(n7sd_5_e), .d(n7sd_5_d_2), .c(n7sd_5_c_2));  // open: dp
  _7_Segment_Display u_7_segment_display_7 (
    .g(n7sd_6_g), .f(n7sd_6_f), .a(n7sd_6_a), .b(n7sd_6_b_2), .e(n7sd_6_e), .d(n7sd_6_d_2), .c(n7sd_6_c_2));  // open: dp
  _7_Segment_Display u_7_segment_display_8 (
    .g(n7sd_8_g), .f(n7sd_8_f), .a(n7sd_8_a), .b(n7sd_8_b_2), .e(n7sd_8_e), .d(n7sd_8_d_2), .c(n7sd_8_c_2));  // open: dp
  _7_Segment_Display u_7_segment_display_9 (
    .g(n7sd_7_g), .f(n7sd_7_f), .a(n7sd_7_a), .b(n7sd_7_b_2), .e(n7sd_7_e), .d(n7sd_7_d_2), .c(n7sd_7_c_2));  // open: dp
  _7SD u_7sd_7 (
    .in_1(R3), .B(R2), .C(R1), .D(R0), .a(n7sd_7_a), .b_2(n7sd_7_b_2), .c_2(n7sd_7_c_2), .d_2(n7sd_7_d_2),
    .e(n7sd_7_e), .f(n7sd_7_f), .g(n7sd_7_g));
  _7SD u_7sd_8 (
    .in_1(Q3), .B(Q2), .C(Q1), .D(Q0), .a(n7sd_8_a), .b_2(n7sd_8_b_2), .c_2(n7sd_8_c_2), .d_2(n7sd_8_d_2),
    .e(n7sd_8_e), .f(n7sd_8_f), .g(n7sd_8_g));

  // Other names for the same wires on the sheet: B1 = in_16; B2 = in_15; B3 = in_14; B4 = in_13; B5 = in_12;
  //   B6 = in_11; B7 = in_10; B8 = in_9; A1 = in_8; A2 = in_7; A3 = in_6; A4 = in_5; A5 = in_4; A6 = in_3; A7 = in_2;
  //   A8 = in_1

  // Notes on the sheet:
  //   Separate Display for Division
  //   00 - Addition
  //   01 - Subtraction
  //   10 - Multiplication
  //   Keep this Always On
  //   Subtraction and Division are with respect to B numbered bits
  //   Dhanvanshikumar Hanchate
  //   BT23CSE113
  //   Multiplier
  //   Sign
  //   3rd Bit
  //   2nd Bit
  //   1st Bit
  //   0th Bit
  //   DIVISOR
  //   Keep this Always On
  //   Quotient
  //   Remainder
endmodule

module _7SD (
  input  in_1,
  input  B,
  input  C,
  input  D,
  output a,
  output b_2,
  output c_2,
  output d_2,
  output e,
  output f,
  output g
);

  wire and_1_out, and_2_out, and_3_out, and_4_out, and_5_out, and_6_out, and_7_out, and_8_out, and_9_out,
       and_10_out, and_11_out, and_12_out, and_13_out, and_14_out, and_15_out, and_16_out, and_17_out,
       and_18_out, and_19_out, and_20_out, and_21_out, and_22_out, and_23_out, and_24_out, and_25_out,
       and_26_out, and_27_out, and_28_out, and_29_out, and_30_out, and_31_out, and_32_out, and_33_out,
       and_34_out, and_35_out, not_1_out, not_2_out, not_3_out, not_4_out, not_5_out, not_6_out, not_7_out,
       not_8_out, not_9_out, not_10_out, not_11_out, not_12_out, not_13_out, not_14_out, not_15_out,
       not_16_out, not_17_out, not_18_out, not_19_out, not_20_out, not_21_out, not_22_out, not_23_out,
       not_24_out, not_25_out, not_26_out, not_27_out, not_28_out, not_29_out, not_30_out, not_31_out,
       not_32_out, not_33_out, not_34_out, not_35_out, not_36_out, not_37_out, not_38_out, not_39_out,
       not_40_out, not_41_out, not_42_out, not_43_out;

  not not_1 (not_1_out, B);
  and and_1 (and_1_out, not_1_out, not_2_out);
  not not_2 (not_2_out, D);
  not not_3 (not_3_out, in_1);
  and and_2 (and_2_out, not_3_out, C);
  not not_4 (not_4_out, in_1);
  and and_3 (and_3_out, not_4_out, B, D);
  and and_4 (and_4_out, B, C);
  and and_5 (and_5_out, in_1, not_5_out, not_6_out);
  not not_5 (not_5_out, B);
  not not_6 (not_6_out, C);
  and and_6 (and_6_out, in_1, not_7_out);
  not not_7 (not_7_out, D);
  not not_8 (not_8_out, in_1);
  and and_7 (and_7_out, not_8_out, not_9_out);
  not not_9 (not_9_out, B);
  not not_10 (not_10_out, in_1);
  not not_11 (not_11_out, C);
  and and_8 (and_8_out, not_10_out, not_11_out, not_12_out);
  not not_12 (not_12_out, D);
  not not_13 (not_13_out, B);
  and and_9 (and_9_out, not_13_out, not_14_out);
  not not_14 (not_14_out, D);
  not not_15 (not_15_out, in_1);
  and and_10 (and_10_out, not_15_out, C, D);
  not not_16 (not_16_out, C);
  and and_11 (and_11_out, in_1, not_16_out, D);
  not not_17 (not_17_out, in_1);
  and and_12 (and_12_out, not_17_out, not_18_out);
  not not_18 (not_18_out, C);
  not not_19 (not_19_out, in_1);
  and and_13 (and_13_out, not_19_out, D);
  not not_20 (not_20_out, C);
  and and_14 (and_14_out, not_20_out, D);
  not not_21 (not_21_out, in_1);
  and and_15 (and_15_out, not_21_out, B);
  and and_16 (and_16_out, in_1, not_22_out);
  not not_22 (not_22_out, B);
  not not_23 (not_23_out, in_1);
  and and_17 (and_17_out, not_23_out, not_24_out, not_25_out);
  not not_24 (not_24_out, B);
  not not_25 (not_25_out, D);
  not not_26 (not_26_out, B);
  and and_18 (and_18_out, not_26_out, C, D);
  and and_19 (and_19_out, B, not_27_out, D);
  not not_27 (not_27_out, C);
  and and_20 (and_20_out, B, C, not_28_out);
  not not_28 (not_28_out, D);
  and and_21 (and_21_out, in_1, not_29_out);
  not not_29 (not_29_out, C);
  not not_30 (not_30_out, B);
  and and_22 (and_22_out, not_30_out, not_31_out);
  not not_31 (not_31_out, D);
  and and_23 (and_23_out, C, not_32_out);
  not not_32 (not_32_out, D);
  and and_24 (and_24_out, in_1, C);
  and and_25 (and_25_out, in_1, B);
  not not_33 (not_33_out, C);
  and and_26 (and_26_out, not_33_out, not_34_out);
  not not_34 (not_34_out, D);
  not not_35 (not_35_out, in_1);
  and and_27 (and_27_out, not_35_out, B, not_36_out);
  not not_36 (not_36_out, C);
  and and_28 (and_28_out, B, not_37_out);
  not not_37 (not_37_out, D);
  and and_29 (and_29_out, in_1, not_38_out);
  not not_38 (not_38_out, B);
  and and_30 (and_30_out, in_1, C);
  not not_39 (not_39_out, B);
  and and_31 (and_31_out, not_39_out, C);
  and and_32 (and_32_out, C, not_40_out);
  not not_40 (not_40_out, D);
  not not_41 (not_41_out, in_1);
  and and_33 (and_33_out, not_41_out, B, not_42_out);
  not not_42 (not_42_out, C);
  and and_34 (and_34_out, in_1, not_43_out);
  not not_43 (not_43_out, B);
  and and_35 (and_35_out, in_1, D);
  or or_1 (b_2, and_7_out, and_8_out, and_9_out, and_10_out, and_11_out);
  or or_2 (c_2, and_12_out, and_13_out, and_14_out, and_15_out, and_16_out);
  or or_3 (d_2, and_17_out, and_18_out, and_19_out, and_20_out, and_21_out);
  or or_4 (e, and_22_out, and_23_out, and_24_out, and_25_out);
  or or_5 (f, and_26_out, and_27_out, and_28_out, and_29_out, and_30_out);
  or or_6 (g, and_31_out, and_32_out, and_33_out, and_34_out, and_35_out);
  or or_7 (a, and_1_out, and_2_out, and_3_out, and_4_out, and_5_out, and_6_out);
endmodule
